// Logisim project cpu.circ as structural Verilog: 1 circuit, main circuit cpu
module cpu (
  input  clk,
  input  [31:0] INSTRUCTION,
  input  [31:0] READ_DATA,
  output [31:0] WRITE_ADDRESS,
  output [31:0] PROGRAM_COUNTER,
  output [31:0] ra,
  output [31:0] sp,
  output [31:0] t0,
  output [31:0] t1,
  output [31:0] t2,
  output [31:0] s0,
  output [31:0] s1,
  output [31:0] a0,
  output [31:0] tohost,
  output [3:0] WRITE_ENABLE,
  output [31:0] WRITE_DATA,
  output [31:0] out_17,
  output [31:0] out_18,
  output [31:0] out_19,
  output [4:0] out_20,
  output [4:0] out_21,
  output [31:0] out_22
);

  wire [1:0] WBSel;
  wire [2:0] ImmSel;
  wire [31:0] adder_1_out, read_data_1;

  Adder #(.width(32)) adder_1 (.a(PROGRAM_COUNTER), .b(32'h4), .out(adder_1_out));  // open: cin, cout
  Register #(.width(32)) PC (.D(adder_1_out), .clk(clk), .Q(PROGRAM_COUNTER));  // open: en, clr
  Register #(.width(32)) instEX (.D(INSTRUCTION), .clk(clk), .Q(out_17));  // open: en, clr
  control_logic control_logic_1 (
    .ImmSel(ImmSel), .WBSel(WBSel), .inst(INSTRUCTION));  // open: CSRWen, PCSel, RegWEn, BrUn, ASel, BSel, ALUSel, MemRW, CSRSel, BrEq, BrLt
  imm_gen imm_gen_1 (.inst(out_17), .ImmSel(ImmSel), .imm(out_18));
  regfile regfile_1 (
    .rs1(out_17[19:15]), .rd(out_17[11:7]), .Write_Data(out_19), .RegWEn(1'b1), .clk(clk), .ra(ra), .sp(sp),
    .t0(t0), .t1(t1), .t2(t2), .s0(s0), .s1(s1), .a0(a0), .Read_Data_1(read_data_1));  // open: rs2, Read_Data_2
  // branch_comp branch_comp_1: pin names not known
  alu alu_1 (.Result(out_22), .A(read_data_1), .B(out_18), .ALUSel(4'b0000));
  csr csr_1 (.tohost(tohost));  // open: CSR_address, CSR_din, CSR_WE, clk
  Multiplexer #(.enable("false"), .select(2), .width(32)) multiplexer_1 (
    .in0(out_22), .in2(PROGRAM_COUNTER), .out(out_19), .sel(WBSel));  // open: in1, in3

  assign out_20 = out_17[19:15];
  assign out_21 = out_17[11:7];
  // also tied to GND on the sheet: {WBSel[0], WBSel[1]}

  // Other names for the same wires on the sheet: alu_result[31:0] = out_22; imm[31:0] = out_18; instEX[31:0] = out_17;
  //   Opcode[6:0] = out_17[6:0]; rd[4:0] = out_17[11:7]; funct3[2:0] = out_17[14:12]; rs1[4:0] = out_17[19:15];
  //   reg_write_data[31:0] = out_19

  // Notes on the sheet:
  //   Output to IMEM
  //   IMEM (do **NOT** move this)
  //   Inputs from IMEM
  //   It is OK to move the PC, RegFile, ALU, MEM, Branch Comp, Imm Gen, and Control Logic to wherever is most convenient for you when constructing your CPU, and to delete this text
  //   Inputs/Outputs for testing. Do **NOT** move these.
  //   Outputs To DMEM
  //   DMEM (do **NOT** move this)
  //   Inputs From DMEM
endmodule
